# Fritzing sketch diffbot (saved by Fritzing 0.9.4)

parts:
  DG01D-E_Motor_with_Encoder1 = Hobby Motor with Encoder - Metal Gear (DG01D-E) [part_number=VT-E-G25A-06-177E]  # not connected
  DG01D-E_Motor_with_Encoder2 = Hobby Motor with Encoder - Metal Gear (DG01D-E) [part_number=VT-E-G25A-06-177E]  # not connected
  Teensy1 = Teensy 4.0  # not connected
  Mod1 = Raspberry Pi 4B  # not connected
  USBTTL1 = Micro USB B Plug
  USBTTL2 = USB A Plug

nets:
  N1: USBTTL1.usb, USBTTL2.usb

custom parts:
  Hobby Motor with Encoder - Metal Gear (DG01D-E): The DG01D-E is a single hobby motor with a hall speed encoder. This motor requires a voltage between 3-9V, has a gearbox ratio of 1:48 and a speed of 90RPM at 4.5V. The voltage between positive and negative is determined according to the power supply voltage of the single chip microcomputer used, generally 3.3V or 5V is used. The hall sensor can sense the North and South poles of its magnetic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
  Teensy 4.0: The Teensy is a complete USB-based microcontoller development system, in a very small footprint, capable of implementing many types of projects. All programming is done via the USB port. No special programmer is needed, only a standard micro-USB cable and a PC or Macintosh with a USB port.
  Micro USB B Plug: Micro USB B Plug breadboard only for documetnation purposes.
  USB A Plug: USB A Plug breadboard only for documetnation purposes.
